# Fritzing sketch Feather-AdaLogger (saved by Fritzing 0.9.10b)

parts:
  Part16 = Adafruit Feather M0 Adalogger [part_number="Adafruit #2796"]
  BAT1 = Battery Holders [package=lipo-1100mAh]  # not connected
  Part18 = Adafruit DS3231 STEMMA QT [part_number="Adafruit #5188"]
  Part21 = Adafruit BMP280 [part_number="Adafruit #2651"]  # not connected
  Part22 = Adafruit BMP388 [part_number="Adafruit #3966"]  # not connected
  Part23 = Adafruit BME280 [part_number="Adafruit #2652"]  # not connected
  Part25 = Adafruit HTU21D-F Temperature & Humidity Sensor [part_number="Adafruit #1899"]  # not connected
  Part26 = Adafruit MCP9808 [part_number="Adafruit #5027"]  # not connected
  Part27 = SI1145 Digital UV Index + IR + Visible Light Sensor [part_number=1777]  # not connected
  OLED_I2C4 = OLED 128x64 I2C Monochrome Display  # not connected
  Part28 = OLED Monochrome 128x32 I2C [part_number=931]  # not connected
  U8 = Honeywell SS451A [chip_label="Hall Effect Sensor" package=THT]
  U9 = Honeywell SS451A [chip_label="Hall Effect Sensor" package=THT]
  R20 = Resistor [tolerance=±5% resistance=1k power=0.25 package=THT]
  R21 = Resistor [tolerance=±5% resistance=1k power=0.25 package=THT]
  C3 = Ceramic Capacitor [capacitance=0.1mF voltage=35V package="100 mil [THT, multilayer]"]
  C4 = Ceramic Capacitor [capacitance=0.1mF package="100 mil [THT, multilayer]"]

nets:
  GND: Part16.GND, Part16.D12, Part18.GND, U8.pin2, U9.pin2, C3.0, C4.0
  N1: Part16.A3, U8.pin3
  N2: Part16.A2, U9.pin3
  N3: Part16.SCL, Part18.SCL
  N4: Part16.SDA, Part18.SDA
  N5: U8.pin1, U9.pin1, R20.Pin_0, C3.1
  N6: R21.Pin_0, C4.1

notes:
  Feather AdaLogger - No Network, SD Card Only
  Feather AdaLogger Full Station
  v2025-05-25
  Feather SD
  Pin - D4 SD CS
  Pin - SPI MOSI
  Pin - SPI MISO
  Pin - SPI CLK
  Console Enable Jumper
  Jump Pin 12 to Ground
  Snow & Stream Gauge A4
  Adafruit DS3231
  RTC
  I2C 7-bit address 0x68
  BMP280
  Barometic Pressure
  Altitude Sensor
  Temperature
  I2C 7-bit address
  Default = 0x77
  SD0 to GND = 0x76
  BMP388
  Barometic Pressure
  Altitude Sensor
  Temperature
  I2C 7-bit address
  Default = 0x77
  SD0 to GND = 0x76
  BME288
  Barometic Pressure
  Altitude Sensor
  Temperature
  Humidity
  I2C 7-bit address
  Default = 0x76
  SD0 to GND = 0x77
  HTU21D-F Temperature & Humidity Sensor
  I2C 7-bit address 0x40
  MCP9808 High Accuracy Temperature Sensor
  I2C 7-bit address 0x18
  Adafruit SI1145
  Light Sensor
  I2C 7-bit address 0x60
  Adafruit OLED64
  Display SSD1306
  I2C 7-bit address 0x3D
  Adafruit OLED 128x32
  Display SSD1306
  I2C 7-bit address 0x3C
  Rain Gauge 1 (A3)
  SS451A Omnipolar Digital Hall-effect Sensor
  Anemometer (A2)
  SS451A Omnipolar Digital Hall-effect Sensor
  D8 = Serial Console (Ground Pin to Enable)
  D7 = On Board LED - Unused - Not on Grove Shield
  D6 =
  D5 =
  D4 = SD Card Chip Select
  D3 =
  D2 =
  D1 = I2C SCL
  D0 = I2C SDA
  A0 = WatchDog Monitor/Relay Reset Trigger (Future)
  A1 = WatchDog Monitor Heartbeat (Future)
  A2 = Interrupt For Anemometer (Wind Speed)
  A3 = Interrupt For Rain Gauge
  A4 = Optional Distance Sensor
  A5 =
  D13 = SPIO CLK SD Card
  D12 = SPI0 MOSI SD Card
  D11 = SPI0 MISO SD Card
  D10 =
  D9 =

custom parts:
  Adafruit Feather M0 Adalogger: This is the Adafruit Feather M0 Adalogger - our take on an 'all-in-one' Cortex M0 datalogger (or data-reader) with built in USB and battery charging. Its an Adafruit Feather M0 with a microSD holder ready to rock! We have other boards in the Feather family, check'em out here At the Feather M0's heart is an ATSAMD21G18 ARM Cortex M0 processor, clocked at 48 MHz and at 3.3V logic, the same one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
  Adafruit DS3231 STEMMA QT: The datasheet for the DS3231 explains that this part is an "Extremely Accurate I²C-Integrated RTC/TCXO/Crystal". And, hey, it does exactly what it says on the tin! This Real Time Clock (RTC) is the most precise you can get in a small, low-power package. We've had a breakout board version of this RTC for a while, but we want to make it even easier for folks to use, so now it comes with STEMMA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
  Adafruit BMP280: Bosch has stepped up their game with their new BMP280 sensor, an environmental sensor with temperature, barometric pressure that is the next generation upgrade to the BMP085/BMP180/BMP183. This sensor is great for all sorts of weather sensing and can even be used in both I2C and SPI! This precision sensor from Bosch is the best low-cost, precision sensing solution for measuring barometric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
  Adafruit BMP388: Bosch has been a leader in barometric pressure sensors, from the BMP085. BMP180, and BMP280... now we've got the next generation, the Adafruit BMP388 Precision Barometric Pressure sensor. As you would expect, this sensor is similar to its earlier versions but even better. The BMP388 has better precision than ever, which makes it excellent for environmental sensing or as a precision altimeter.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
  Adafruit BME280: Bosch has stepped up their game with their new BME280 sensor, an environmental sensor with temperature, barometric pressure and humidity! This sensor is great for all sorts of indoor environmental sensing and can even be used in both I2C and SPI! This precision sensor from Bosch is the best low-cost sensing solution for measuring humidity with ±3% accuracy, barometric pressure with ±1 hPa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
  Adafruit HTU21D-F Temperature & Humidity Sensor: It's summer and you're sweating and your hair's all frizzy and all you really want to know is why the weatherman said this morning that today's relative humidity would max out at a perfectly reasonable 52% when it feels more like 77%. Enter the HTU21D-F Temperature + Humidity Sensor - the best way to prove the weatherman wrong! This I2C digital humidity sensor is an accurate and intelligent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
  Adafruit MCP9808: The MCP9808 digital temperature sensor is one of the more accurate/precise we've ever seen, with a typical accuracy of ±0.25°C over the sensor's -40°C to +125°C range and precision of +0.0625°C. They work great with any microcontroller using standard I2C. With three address jumpers on the back, you can connect up to 8 to a single I2C bus without address collisions. Best of all, a wide voltage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
  SI1145 Digital UV Index + IR + Visible Light Sensor: The SI1145 is a new sensor from SiLabs with a calibrated light sensing algorithm that can calculate UV Index. It doesn't contain an actual UV sensing element, instead it approximates it based on visible & IR light from the sun. We took this outside a couple days and compared the calculated UV index with the news-reported index and found it was very accurate! It's a digital sensor that works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
  OLED Monochrome 128x32 I2C: These displays are small, only about 1" diagonal, but very readable due to the high contrast of an OLED display. This display is made of 128x32 individual white OLED pixels, each one is turned on or off by the controller chip. Because the display makes its own light, no backlight is required. This reduces the power required to run the OLED and is why the display has such high contrast; we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
  Honeywell SS451A: Omnipolar Digital Hall-effect Sensor
